// Logisim project cpu.circ as structural Verilog: 13 circuits, main circuit main
module main (
);

  wire alucontrol_1_branch, and_1_out, Clock, control_unit_1_alusrc, control_unit_1_branch,
       control_unit_1_jump, control_unit_1_memread, control_unit_1_memtoreg, control_unit_1_memwrite,
       control_unit_1_regdest, control_unit_1_regwrite, Reset_2_out, Reset_3_out, Reset_4_out, Reset_5_out,
       Reset_out;
  wire [4:0] multiplexer_1_out;
  wire [5:0] alucontrol_1_opcode, control_unit_1_opcodeout;
  wire [7:0] bit_extender_4_out;
  wire [15:0] alu_1_output, bit_extender_1_out, multiplexer_2_out, multiplexer_5_out, ram_1_data, ram_2_data,
       register_file_1_data_addr_1_out, register_file_1_data_addr_2_out;
  wire [31:0] _32_bit_adder_output, bit_extender_2_out, bit_extender_3_out, counter_1_q, multiplexer_3_out,
       multiplexer_4_out;
  wire [31:16] ram_1_data_2;

  Clock clock_1 (.out(Clock));
  Counter #(.width(32), .max('hffffffff)) counter_1 (
    .load(1'b1), .D(multiplexer_4_out), .count(1'b0), .Q(counter_1_q), .clk(Clock), .clr(Reset_out));  // open: carry
  Button Reset (.out(Reset_out));
  _32_bit_adder _32_bit_adder (.A(counter_1_q), .B(32'h1), .Output(_32_bit_adder_output));
  Bit_Extender #(.in_width(32), .\type ("sign")) bit_extender_1 (.in(counter_1_q), .out(bit_extender_1_out));
  RAM #(.addrWidth(16), .dataWidth(32)) ram_1 (
    .addr(bit_extender_1_out), .data({ram_1_data_2, ram_1_data}), .sel(1'b1), .clk(Clock), .ld(1'b1),
    .clr(Reset_2_out));
  Button Reset_2 (.out(Reset_2_out));
  Multiplexer #(.width(5)) multiplexer_1 (
    .in0(ram_1_data_2[20:16]), .in1(ram_1_data[15:11]), .out(multiplexer_1_out), .sel(control_unit_1_regdest));  // open: en
  control_unit control_unit_1 (
    .Opcode(ram_1_data_2[31:26]), .Jump(control_unit_1_jump), .Branch(control_unit_1_branch),
    .MemRead(control_unit_1_memread), .MemToReg(control_unit_1_memtoreg), .MemWrite(control_unit_1_memwrite),
    .ALUSrc(control_unit_1_alusrc), .RegWrite(control_unit_1_regwrite), .RegDest(control_unit_1_regdest),
    .OpcodeOUT(control_unit_1_opcodeout));
  assign bit_extender_2_out = {{6{ram_1_data_2[25]}}, {ram_1_data_2[25:16], ram_1_data}};  // Bit_Extender bit_extender_2
  Register_File register_file_1 (
    .Write_Data_Input(multiplexer_5_out), .Load(control_unit_1_regwrite), .Read_Addr_1(ram_1_data_2[25:21]),
    .Reset(Reset_3_out), .Clock(Clock), .Write_Data_Register_Address(multiplexer_1_out),
    .Read_Addr_2(ram_1_data_2[20:16]), .Data_Addr_1_out(register_file_1_data_addr_1_out),
    .Data_Addr_2_out(register_file_1_data_addr_2_out));
  Button Reset_3 (.out(Reset_3_out));
  assign bit_extender_3_out = {{16{ram_1_data[15]}}, ram_1_data};  // Bit_Extender bit_extender_3
  Multiplexer #(.width(16)) multiplexer_2 (
    .in0(register_file_1_data_addr_2_out), .in1(ram_1_data), .out(multiplexer_2_out),
    .sel(control_unit_1_alusrc));  // open: en
  ALUControl alucontrol_1 (
    .Opcode_Input(control_unit_1_opcodeout), .A(register_file_1_data_addr_1_out),
    .B(register_file_1_data_addr_2_out), .Opcode(alucontrol_1_opcode), .Branch(alucontrol_1_branch));
  ALU alu_1 (
    .A(register_file_1_data_addr_1_out), .B(multiplexer_2_out), .Opcode(alucontrol_1_opcode), .Clock(Clock),
    .Output(alu_1_output), .Reset(Reset_4_out));
  Button Reset_4 (.out(Reset_4_out));
  Multiplexer #(.width(32)) multiplexer_3 (
    .in0(_32_bit_adder_output), .in1(bit_extender_3_out), .out(multiplexer_3_out), .sel(and_1_out));  // open: en
  and and_1 (and_1_out, alucontrol_1_branch, control_unit_1_branch);
  Bit_Extender #(.in_width(16), .out_width(8), .\type ("sign")) bit_extender_4 (
    .in(alu_1_output), .out(bit_extender_4_out));
  Multiplexer #(.width(32)) multiplexer_4 (
    .in0(multiplexer_3_out), .in1(bit_extender_2_out), .out(multiplexer_4_out), .sel(control_unit_1_jump));  // open: en
  RAM #(.dataWidth(16), .bus("separate")) ram_2 (
    .addr(bit_extender_4_out), .din(register_file_1_data_addr_2_out), .data(ram_2_data),
    .str(control_unit_1_memwrite), .sel(1'b1), .clk(Clock), .ld(control_unit_1_memread), .clr(Reset_5_out));
  Button Reset_5 (.out(Reset_5_out));
  Multiplexer #(.width(16)) multiplexer_5 (
    .in0(alu_1_output), .in1(ram_2_data), .out(multiplexer_5_out), .sel(control_unit_1_memtoreg));  // open: en

  // Notes on the sheet:
  //   Instruction Memory
  //   Control Unit
  //   Data Memory
endmodule

module _1_bit_adder (
  input  A,
  input  B,
  input  Cin,
  output S,
  output Cout
);

  wire and_1_out, and_2_out, xor_1_out;

  xor xor_1 (xor_1_out, A, B);
  xor xor_2 (S, xor_1_out, Cin);
  and and_1 (and_1_out, xor_1_out, Cin);
  and and_2 (and_2_out, A, B);
  or or_1 (Cout, and_1_out, and_2_out);
endmodule

// Adder
module _16_bit_adder (
  input  CIN,
  input  [15:0] A,
  input  [15:0] B,
  output [15:0] Sum,
  output Cout
);

  wire n1_bit_adder_1_cout, n1_bit_adder_2_cout, n1_bit_adder_3_cout, n1_bit_adder_4_cout,
       n1_bit_adder_5_cout, n1_bit_adder_6_cout, n1_bit_adder_7_cout, n1_bit_adder_8_cout,
       n1_bit_adder_9_cout, n1_bit_adder_10_cout, n1_bit_adder_11_cout, n1_bit_adder_12_cout,
       n1_bit_adder_13_cout, n1_bit_adder_14_cout, n1_bit_adder_15_cout;

  _1_bit_adder u_1_bit_adder_1 (.A(A[0]), .B(B[0]), .Cin(CIN), .S(Sum[0]), .Cout(n1_bit_adder_1_cout));
  _1_bit_adder u_1_bit_adder_2 (.A(A[1]), .B(B[1]), .Cin(n1_bit_adder_1_cout), .S(Sum[1]), .Cout(n1_bit_adder_2_cout));
  _1_bit_adder u_1_bit_adder_3 (.A(A[2]), .B(B[2]), .Cin(n1_bit_adder_2_cout), .S(Sum[2]), .Cout(n1_bit_adder_3_cout));
  _1_bit_adder u_1_bit_adder_4 (.A(A[3]), .B(B[3]), .Cin(n1_bit_adder_3_cout), .S(Sum[3]), .Cout(n1_bit_adder_4_cout));
  _1_bit_adder u_1_bit_adder_5 (.A(A[4]), .B(B[4]), .Cin(n1_bit_adder_4_cout), .S(Sum[4]), .Cout(n1_bit_adder_5_cout));
  _1_bit_adder u_1_bit_adder_6 (.A(A[5]), .B(B[5]), .Cin(n1_bit_adder_5_cout), .S(Sum[5]), .Cout(n1_bit_adder_6_cout));
  _1_bit_adder u_1_bit_adder_7 (.A(A[6]), .B(B[6]), .Cin(n1_bit_adder_6_cout), .S(Sum[6]), .Cout(n1_bit_adder_7_cout));
  _1_bit_adder u_1_bit_adder_8 (.A(A[7]), .B(B[7]), .Cin(n1_bit_adder_7_cout), .S(Sum[7]), .Cout(n1_bit_adder_8_cout));
  _1_bit_adder u_1_bit_adder_9 (.A(A[8]), .B(B[8]), .Cin(n1_bit_adder_8_cout), .S(Sum[8]), .Cout(n1_bit_adder_9_cout));
  _1_bit_adder u_1_bit_adder_10 (
    .A(A[9]), .B(B[9]), .Cin(n1_bit_adder_9_cout), .S(Sum[9]), .Cout(n1_bit_adder_10_cout));
  _1_bit_adder u_1_bit_adder_11 (
    .A(A[10]), .B(B[10]), .Cin(n1_bit_adder_10_cout), .S(Sum[10]), .Cout(n1_bit_adder_11_cout));
  _1_bit_adder u_1_bit_adder_12 (
    .A(A[11]), .B(B[11]), .Cin(n1_bit_adder_11_cout), .S(Sum[11]), .Cout(n1_bit_adder_12_cout));
  _1_bit_adder u_1_bit_adder_13 (
    .A(A[12]), .B(B[12]), .Cin(n1_bit_adder_12_cout), .S(Sum[12]), .Cout(n1_bit_adder_13_cout));
  _1_bit_adder u_1_bit_adder_14 (
    .A(A[13]), .B(B[13]), .Cin(n1_bit_adder_13_cout), .S(Sum[13]), .Cout(n1_bit_adder_14_cout));
  _1_bit_adder u_1_bit_adder_15 (
    .A(A[14]), .B(B[14]), .Cin(n1_bit_adder_14_cout), .S(Sum[14]), .Cout(n1_bit_adder_15_cout));
  _1_bit_adder u_1_bit_adder_16 (.A(A[15]), .B(B[15]), .Cin(n1_bit_adder_15_cout), .S(Sum[15]), .Cout(Cout));
endmodule

module ALU (
  input  [15:0] A,
  input  [15:0] B,
  input  [5:0] Opcode,
  input  Reset,
  input  Clock,
  output [15:0] Output
);

  wire ADDCARRY, and_1_out, and_3_out, and_4_out, multiplexer_4_out, n16_bit_adder_1_cout, not_1_out,
       not_2_out, not_3_out, not_4_out, not_5_out, not_6_out, not_7_out, not_8_out, not_9_out;
  wire [15:0] and_2_out, MfhiIN, MfhiOUT, MfloIN, MfloOUT, multiplexer_1_out, multiplexer_2_out,
       n16_bit_adder_1_sum, n16_bit_adder_2_sum, or_1_out, Set_less_than_out, shift_left_logical_1_output,
       subtractor_1_out;

  not not_1 (not_1_out, Opcode[0]);
  not not_2 (not_2_out, Opcode[1]);
  not not_3 (not_3_out, Opcode[2]);
  not not_4 (not_4_out, Opcode[5]);
  SLT Set_less_than (.A(A), .B(B), .Out(Set_less_than_out));
  shift_left_logical shift_left_logical_1 (.Input(A), .shamt(B), .\output (shift_left_logical_1_output));
  _16_bit_adder u_16_bit_adder_1 (.CIN(1'b0), .A(B), .B(A), .Sum(n16_bit_adder_1_sum), .Cout(n16_bit_adder_1_cout));
  Subtractor #(.width(16)) subtractor_1 (.a(A), .b(B), .out(subtractor_1_out));  // open: bin, bout
  and and_1 (and_1_out, not_3_out, not_1_out, not_2_out, Opcode[3], Opcode[4], not_4_out);
  assign and_2_out = A & B;  // AND_Gate and_2, 16 bits wide
  assign or_1_out = A | B;  // OR_Gate or_1, 16 bits wide
  MultHiLo multhilo_1 (.A(A), .B(B), .Out_Lo(MfloIN), .Out_Hi(MfhiIN));
  _16_bit_adder u_16_bit_adder_2 (.CIN(ADDCARRY), .A(A), .B(B), .Sum(n16_bit_adder_2_sum));  // open: Cout
  Multiplexer #(.select(5), .width(16)) multiplexer_1 (
    .in0(n16_bit_adder_1_sum), .in2(subtractor_1_out), .in4(and_2_out), .in5(or_1_out),
    .in10(Set_less_than_out), .in31(n16_bit_adder_2_sum), .out(multiplexer_1_out), .sel(Opcode[4:0]));  // open: in1, in3, in6, in7, in8, in9, in11, in12, in13, in14, in15, in16, in17, in18, in19, in20, in21, in22, in23, in24, in25, in26, in27, in28, in29, in30, en
  Multiplexer #(.select(5), .width(16)) multiplexer_2 (
    .in0(shift_left_logical_1_output), .in8(n16_bit_adder_1_sum), .in16(MfhiOUT), .in18(MfloOUT),
    .in24({16{1'b0}}), .out(multiplexer_2_out), .sel(Opcode[4:0]));  // open: in1, in2, in3, in4, in5, in6, in7, in9, in10, in11, in12, in13, in14, in15, in17, in19, in20, in21, in22, in23, in25, in26, in27, in28, in29, in30, in31, en
  not not_5 (not_5_out, Opcode[0]);
  not not_6 (not_6_out, Opcode[1]);
  not not_7 (not_7_out, Opcode[2]);
  not not_8 (not_8_out, Opcode[3]);
  not not_9 (not_9_out, Opcode[4]);
  and and_3 (and_3_out, not_5_out, not_6_out, not_7_out, not_9_out, Opcode[5], not_8_out);
  and and_4 (and_4_out, and_3_out, n16_bit_adder_1_cout);
  Multiplexer #(.width(16)) multiplexer_3 (
    .in0(multiplexer_2_out), .in1(multiplexer_1_out), .out(Output), .sel(Opcode[5]));  // open: en
  Multiplexer multiplexer_4 (.in0(1'b0), .in1(Clock), .out(multiplexer_4_out), .sel(and_1_out));  // open: en
  Register #(.width(16)) mfhi (.D(MfhiIN), .Q(MfhiOUT), .clk(multiplexer_4_out), .clr(Reset));  // open: en
  Register #(.width(16)) mflo (.D(MfloIN), .Q(MfloOUT), .clk(multiplexer_4_out), .clr(Reset));  // open: en
  Register #(.width(1)) HighAdd (.D(and_4_out), .Q(ADDCARRY), .clk(Clock), .clr(Reset));  // open: en
endmodule

module Register_File (
  input  [15:0] Write_Data_Input,
  input  Load,
  input  [4:0] Read_Addr_1,
  input  Reset,
  input  Clock,
  input  [4:0] Write_Data_Register_Address,
  input  [4:0] Read_Addr_2,
  output [15:0] Data_Addr_1_out,
  output [15:0] Data_Addr_2_out
);

  wire and_1_out, and_2_out, and_3_out, and_4_out, and_5_out, and_6_out, and_7_out, and_8_out,
       decoder_1_out0, decoder_1_out1, decoder_1_out2, decoder_1_out3, decoder_1_out4, decoder_1_out5,
       decoder_1_out6, decoder_1_out7;
  wire [15:0] register_1_q, register_2_q, register_3_q, register_4_q, register_5_q, register_6_q,
       register_7_q, register_8_q;

  Decoder #(.select(5)) decoder_1 (
    .out0(decoder_1_out0), .out1(decoder_1_out1), .out2(decoder_1_out2), .out3(decoder_1_out3),
    .out4(decoder_1_out4), .out5(decoder_1_out5), .out6(decoder_1_out6), .out7(decoder_1_out7),
    .sel(Write_Data_Register_Address));  // open: out8, out9, out10, out11, out12, out13, out14, out15, out16, out17, out18, out19, out20, out21, out22, out23, out24, out25, out26, out27, out28, out29, out30, out31, en
  and and_1 (and_1_out, Load, decoder_1_out0);
  and and_2 (and_2_out, Load, decoder_1_out1);
  and and_3 (and_3_out, Load, decoder_1_out2);
  and and_4 (and_4_out, Load, decoder_1_out3);
  Register #(.width(16)) register_1 (.D(Write_Data_Input), .en(and_1_out), .Q(register_1_q), .clk(Clock), .clr(Reset));
  Register #(.width(16)) register_2 (.D(Write_Data_Input), .en(and_2_out), .Q(register_2_q), .clk(Clock), .clr(Reset));
  Register #(.width(16)) register_3 (.D(Write_Data_Input), .en(and_3_out), .Q(register_3_q), .clk(Clock), .clr(Reset));
  Register #(.width(16)) register_4 (.D(Write_Data_Input), .en(and_4_out), .Q(register_4_q), .clk(Clock), .clr(Reset));
  and and_5 (and_5_out, Load, decoder_1_out4);
  and and_6 (and_6_out, Load, decoder_1_out5);
  and and_7 (and_7_out, Load, decoder_1_out6);
  and and_8 (and_8_out, Load, decoder_1_out7);
  Register #(.width(16)) register_5 (.D(Write_Data_Input), .en(and_5_out), .Q(register_5_q), .clk(Clock), .clr(Reset));
  Register #(.width(16)) register_6 (.D(Write_Data_Input), .en(and_6_out), .Q(register_6_q), .clk(Clock), .clr(Reset));
  Register #(.width(16)) register_7 (.D(Write_Data_Input), .en(and_7_out), .Q(register_7_q), .clk(Clock), .clr(Reset));
  Register #(.width(16)) register_8 (.D(Write_Data_Input), .en(and_8_out), .Q(register_8_q), .clk(Clock), .clr(Reset));
  Multiplexer #(.select(5), .width(16)) multiplexer_1 (
    .in0(register_1_q), .in1(register_2_q), .in2(register_3_q), .in3(register_4_q), .in4(register_5_q),
    .in5(register_6_q), .in6(register_7_q), .in7(register_8_q), .out(Data_Addr_1_out), .sel(Read_Addr_1));  // open: in8, in9, in10, in11, in12, in13, in14, in15, in16, in17, in18, in19, in20, in21, in22, in23, in24, in25, in26, in27, in28, in29, in30, in31, en
  Multiplexer #(.select(5), .width(16)) multiplexer_2 (
    .in0(register_1_q), .in1(register_2_q), .in2(register_3_q), .in3(register_4_q), .in4(register_5_q),
    .in5(register_6_q), .in6(register_7_q), .in7(register_8_q), .out(Data_Addr_2_out), .sel(Read_Addr_2));  // open: in8, in9, in10, in11, in12, in13, in14, in15, in16, in17, in18, in19, in20, in21, in22, in23, in24, in25, in26, in27, in28, in29, in30, in31, en
endmodule

// Mult
module MultHiLo (
  input  [15:0] A,
  input  [15:0] B,
  output [15:0] Out_Lo,
  output [15:0] Out_Hi
);

  wire xor_1_out;
  wire [15:0] multiplexer_1_out, multiplexer_2_out, multiplier_1_cout, multiplier_1_out, n16_bit_adder_1_sum,
       n16_bit_adder_2_sum, not_1_out, not_2_out;
  wire [31:0] _32_bit_adder_output, not_3_out;

  _16_bit_adder u_16_bit_adder_1 (.CIN(1'b0), .A(not_1_out), .B(16'h1), .Sum(n16_bit_adder_1_sum));  // open: Cout
  assign not_1_out = ~A;  // NOT_Gate not_1, 16 bits wide
  _16_bit_adder u_16_bit_adder_2 (.CIN(1'b0), .A(not_2_out), .B(16'h1), .Sum(n16_bit_adder_2_sum));  // open: Cout
  assign not_2_out = ~B;  // NOT_Gate not_2, 16 bits wide
  Multiplexer #(.width(16)) multiplexer_1 (
    .in0(A), .in1(n16_bit_adder_1_sum), .out(multiplexer_1_out), .sel(A[15]));  // open: en
  Multiplexer #(.width(16)) multiplexer_2 (
    .in0(B), .in1(n16_bit_adder_2_sum), .out(multiplexer_2_out), .sel(B[15]));  // open: en
  Multiplier #(.width(16)) multiplier_1 (
    .a(multiplexer_1_out), .b(multiplexer_2_out), .out(multiplier_1_out), .cin({16{1'b0}}),
    .cout(multiplier_1_cout));
  xor xor_1 (xor_1_out, A[15], B[15]);
  assign not_3_out = ~{multiplier_1_cout, multiplier_1_out};  // NOT_Gate not_3, 32 bits wide
  Multiplexer #(.width(32)) multiplexer_3 (
    .in0({multiplier_1_cout, multiplier_1_out}), .in1(_32_bit_adder_output), .out({Out_Hi, Out_Lo}),
    .sel(xor_1_out));  // open: en
  _32_bit_adder _32_bit_adder (.A(not_3_out), .B(32'h1), .Output(_32_bit_adder_output));
endmodule

module SLT (
  input  [15:0] A,
  input  [15:0] B,
  output [15:0] Out
);

  wire comparator_1_lt;

  Comparator #(.width(16)) comparator_1 (.a(A), .b(B), .lt(comparator_1_lt));  // open: gt, eq
  assign Out = {{15{1'b0}}, comparator_1_lt};  // Bit_Extender bit_extender_1
endmodule

// sll
module shift_left_logical (
  input  [15:0] Input,
  input  [15:0] shamt,
  output [15:0] \output 
);

  wire or_1_out;
  wire [15:0] shifter_1_out;

  or or_1 (or_1_out, shamt[4], shamt[5], shamt[6], shamt[7], shamt[8], shamt[9], shamt[11], shamt[12], shamt[13], shamt[14], shamt[15], shamt[10]);
  Shifter #(.width(16)) shifter_1 (.in(Input), .\dist (shamt[3:0]), .out(shifter_1_out));
  Multiplexer #(.width(16)) multiplexer_1 (
    .in0(shifter_1_out), .in1({16{1'b0}}), .out(\output ), .sel(or_1_out));  // open: en
endmodule

module beq (
  input  [15:0] A,
  input  [15:0] B,
  output [15:0] out_3
);

  wire comparator_1_eq;

  Comparator #(.width(16)) comparator_1 (.a(A), .b(B), .eq(comparator_1_eq));  // open: gt, lt
  assign out_3 = {{15{1'b0}}, comparator_1_eq};  // Bit_Extender bit_extender_1
endmodule

module blez (
  input  [15:0] A,
  output out_2
);

  wire comparator_1_eq, comparator_1_lt;

  Comparator #(.width(16)) comparator_1 (
    .a(A), .b({16{1'b0}}), .eq(comparator_1_eq), .lt(comparator_1_lt));  // open: gt
  or or_1 (out_2, comparator_1_eq, comparator_1_lt);
endmodule

module ALUControl (
  input  [5:0] Opcode_Input,
  input  [15:0] A,
  input  [15:0] B,
  output [5:0] Opcode,
  output Branch
);

  wire bit_extender_1_out, blez_1_out_2;
  wire [5:0] multiplexer_2_out, multiplexer_3_out;
  wire [15:0] beq_1_out_3;

  beq beq_1 (.A(A), .B(B), .out_3(beq_1_out_3));
  blez blez_1 (.A(A), .out_2(blez_1_out_2));
  Bit_Extender #(.in_width(16), .out_width(1), .\type ("sign")) bit_extender_1 (
    .in(beq_1_out_3), .out(bit_extender_1_out));
  Multiplexer multiplexer_1 (
    .in0(bit_extender_1_out), .in1(blez_1_out_2), .out(Branch), .sel(Opcode_Input[1]));  // open: en
  Multiplexer #(.select(5), .width(6)) multiplexer_2 (
    .in0(Opcode_Input), .in2(Opcode_Input), .in3(6'b100000), .in4(Opcode_Input), .in6(Opcode_Input),
    .in10(Opcode_Input), .in11(6'b100000), .in31(Opcode_Input), .out(multiplexer_2_out),
    .sel(Opcode_Input[4:0]));  // open: in1, in5, in7, in8, in9, in12, in13, in14, in15, in16, in17, in18, in19, in20, in21, in22, in23, in24, in25, in26, in27, in28, in29, in30, en
  Multiplexer #(.select(5), .width(6)) multiplexer_3 (
    .in0(Opcode_Input), .in2(Opcode_Input), .in4(6'b100010), .in6(6'b100010), .in8(Opcode_Input),
    .in16(Opcode_Input), .in18(Opcode_Input), .in24(Opcode_Input), .out(multiplexer_3_out),
    .sel(Opcode_Input[4:0]));  // open: in1, in3, in5, in7, in9, in10, in11, in12, in13, in14, in15, in17, in19, in20, in21, in22, in23, in25, in26, in27, in28, in29, in30, in31, en
  Multiplexer #(.width(6)) multiplexer_4 (
    .in0(multiplexer_3_out), .in1(multiplexer_2_out), .out(Opcode), .sel(Opcode_Input[5]));  // open: en

  // Notes on the sheet:
  //   I type/Sub
  //   I type/Add
endmodule

module control_unit (
  input  [5:0] Opcode,
  output Jump,
  output Branch,
  output MemRead,
  output MemToReg,
  output MemWrite,
  output ALUSrc,
  output RegWrite,
  output RegDest,
  output [5:0] OpcodeOUT
);

  wire [7:0] multiplexer_1_out, multiplexer_2_out;

  Multiplexer #(.select(5), .width(8)) multiplexer_1 (
    .in0(8'hc0), .in2(8'h1), .in4(8'h2), .in7(8'h2), .in8(8'h60), .in16(8'hc0), .in18(8'hc0),
    .in24({8{1'b0}}), .out(multiplexer_1_out), .sel(Opcode[4:0]));  // open: in1, in3, in5, in6, in9, in10, in11, in12, in13, in14, in15, in17, in19, in20, in21, in22, in23, in25, in26, in27, in28, in29, in30, in31, en
  Multiplexer #(.select(5), .width(8)) multiplexer_2 (
    .in0(8'hc0), .in2(8'hc0), .in3(8'h6c), .in4(8'hc0), .in5(8'hc0), .in10(8'hc0), .in11(8'h78),
    .in31(8'hc0), .out(multiplexer_2_out), .sel(Opcode[4:0]));  // open: in1, in6, in7, in8, in9, in12, in13, in14, in15, in16, in17, in18, in19, in20, in21, in22, in23, in24, in25, in26, in27, in28, in29, in30, en
  Multiplexer #(.width(8)) multiplexer_3 (
    .in0(multiplexer_1_out), .in1(multiplexer_2_out),
    .out({RegDest, RegWrite, ALUSrc, MemWrite, MemToReg, MemRead, Branch, Jump}), .sel(Opcode[5]));  // open: en

  assign OpcodeOUT = Opcode;
endmodule

module _32_bit_adder (
  input  [31:0] A,
  input  [31:0] B,
  output [31:0] Output
);

  wire n16_bit_adder_1_cout;

  _16_bit_adder u_16_bit_adder_1 (
    .CIN(1'b0), .A(A[15:0]), .B(B[15:0]), .Sum(Output[15:0]), .Cout(n16_bit_adder_1_cout));
  _16_bit_adder u_16_bit_adder_2 (
    .CIN(n16_bit_adder_1_cout), .A(A[31:16]), .B(B[31:16]), .Sum(Output[31:16]));  // open: Cout
endmodule
